# Fritzing sketch LCD-breadboard-node (saved by Fritzing 0.9.2b)
breadboards: 2

parts:
  LCD1 = LCD screen
  Part1 = Arduino Uno (Rev3)
  R1 = TRIMPOT [package=3362u-2]
  S1 = Pushbutton [package="[SMD]"]
  S2 = Pushbutton [package="[SMD]"]
  S3 = Pushbutton [package="[SMD]"]
  R2 = Resistor [tolerance=±5% resistance=10k package="0603 [SMD]"]
  R3 = Resistor [tolerance=±5% resistance=10k package="0603 [SMD]"]
  R4 = Resistor [tolerance=±5% resistance=10k package="0603 [SMD]"]
  R5 = Resistor [tolerance=±5% resistance=10k package="0603 [SMD]"]
  R6 = Resistor [tolerance=±5% resistance=10k package="0603 [SMD]"]
  R7 = Resistor [tolerance=±5% resistance=10k package="0603 [SMD]"]
  R8 = Resistor [tolerance=±5% resistance=10k package="0603 [SMD]"]
  U1 = atmega328 [package=dip]
  XTAL2 = Crystal [frequency="16 Mhz" package=THT]
  C1 = Capacitor [package=cap-pth-small2]
  C2 = Capacitor [package=cap-pth-small2]

nets:
  VSS: LCD1.VSS, LCD1.R/W, LCD1.LED-, Part1.GND, R1.CCW, R5.Pin_1, R6.Pin_1, U1.GND#7, C1.2, C2.1
  VDD: LCD1.VDD, LCD1.LED+, Part1.5V, R1.CW, R4.Pin_0, R7.Pin_0, R8.Pin_0, U1.VCC
  N1: LCD1.V0, R1.WIPER
  N2: LCD1.RS, Part1.D4
  N3: LCD1.E, Part1.D5_PWM
  N4: LCD1.DB4, Part1.D6_PWM
  N5: LCD1.DB5, Part1.D7
  N6: LCD1.DB6, Part1.D8
  N7: LCD1.DB7, Part1.D9_PWM
  N8: Part1.A0, S1.Pin_1, S1.Pin_2, S2.Pin_1, S2.Pin_2, S3.Pin_1, S3.Pin_2, R6.Pin_0
  N9: Part1.A4/SDA, R8.Pin_1, U1.A4
  N10: Part1.A5/SCL, R7.Pin_1, U1.A5
  N11: S1.Pin_3, S1.Pin_4, R2.Pin_0, R4.Pin_1
  N12: S2.Pin_3, S2.Pin_4, R2.Pin_1, R3.Pin_0
  N13: S3.Pin_3, S3.Pin_4, R3.Pin_1, R5.Pin_0
  N14: U1.XLAT1, XTAL2.pin_1, C1.1
  N15: U1.XLAT2, XTAL2.pin_0, C2.2
